# Fritzing sketch WorldMap (saved by Fritzing 0.9.9b)

parts:
  LED1 = LED - 5mm [color="White (4500K)" current=0.030 package="5 mm [THT]"]
  LED2 = LED - 5mm [color="White (4500K)" current=0.030 package="5 mm [THT]"]
  WeMos_D1_Mini1 = WeMos D1 Mini
  Part1 = TXB0108 8-channel Bi-directional Logic Level Converter
  LED3 = LED - 5mm [color="White (4500K)" current=0.030 package="5 mm [THT]"]
  LED4 = LED - 5mm [color="White (4500K)" current=0.030 package="5 mm [THT]"]
  LED5 = LED - 5mm [color="White (4500K)" current=0.030 package="5 mm [THT]"]
  U1 = POT [package=pot_alpha_rv16af-20]
  R1 = Resistor [tolerance=±5% resistance=220 package="0603 [SMD]"]
  Mod1 = KY-003 Hall Magnetic Sensor Module [package="Breakout board"]
  Mod2 = KY-003 Hall Magnetic Sensor Module [package="Breakout board"]
  Mod3 = KY-003 Hall Magnetic Sensor Module [package="Breakout board"]
  Mod4 = KY-003 Hall Magnetic Sensor Module [package="Breakout board"]
  Mod5 = KY-003 Hall Magnetic Sensor Module [package="Breakout board"]

nets:
  N1: LED1.cathode, LED2.cathode, WeMos_D1_Mini1.G, Part1.GND, LED3.cathode, LED4.cathode, LED5.cathode
  N2: LED1.anode, LED2.anode, LED3.anode, LED4.anode, LED5.anode, U1.A
  N3: WeMos_D1_Mini1.3V3, Part1.VCCB
  N4: WeMos_D1_Mini1.5V, Part1.VCCA
  N5: WeMos_D1_Mini1.D0, Part1.B2
  N6: WeMos_D1_Mini1.D4, Part1.B1
  N7: WeMos_D1_Mini1.D5, Part1.B3
  N8: WeMos_D1_Mini1.D6, Part1.B4
  N9: WeMos_D1_Mini1.D7, Part1.B5
  N10: WeMos_D1_Mini1.D8, Part1.B6
  N11: Part1.A6, R1.Pin_1
  N12: Part1.A5, Mod5.S
  N13: Part1.A4, Mod4.S
  N14: Part1.A3, Mod3.S
  N15: Part1.A2, Mod2.S
  N16: Part1.A1, Mod1.S
  N17: U1.S, R1.Pin_0
  N18: Mod1.-, Mod2.-, Mod3.-, Mod4.-, Mod5.-
  VIN: Mod1.Vin, Mod2.Vin, Mod3.Vin, Mod4.Vin, Mod5.Vin

custom parts:
  TXB0108 8-channel Bi-directional Logic Level Converter: Because the Arduino (and Basic Stamp) are 5V devices, and most modern sensors, displays, flash cards and modes are 3.3V-only, many makers find that they need to perform level shifting/conversion to protect the 3.3V device from 5V. Although one can use resistors to make a divider, for high speed transfers, the resistors can add a lot of slew and cause havoc that is tough to debug. For that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
  KY-003 Hall Magnetic Sensor Module: KEYES KY-003 Arduino Hall Magnetic Sensor Module is a switch that will turn on/off in the presence of a magnetic field.
